// Logisim project ALU.circ as structural Verilog: 3 circuits, main circuit ALU
module ALU (
  input  [3:0] Codop,
  input  [31:0] A,
  input  [31:0] B,
  input  [4:0] Shift,
  input  CarryIn,
  output [31:0] S,
  output [3:0] Flags
);

  wire ADC_OUT, bitselector_1_out, bitselector_2_out, bitselector_3_out, bitselector_4_out,
       bitselector_5_out, CMN_OUT, CMP_OUT, not_1_out, RSB_OUT, SBC_OUT, v_flag_add_1_v, v_flag_sub_1_v;
  wire [4:0] subtractor_4_out, subtractor_5_out;
  wire [31:0] adder_1_out, and_1_out, and_3_out, CMN, multiplier_1_out, not_2_out, not_3_out, or_1_out,
       shifter_1_out, shifter_2_out, shifter_3_out, shifter_4_out, subtractor_1_out, subtractor_2_out,
       xor_1_out;

  not not_1 (not_1_out, CarryIn);
  assign not_2_out = ~A;  // NOT_Gate not_2, 32 bits wide
  assign and_1_out = A & B;  // AND_Gate and_1, 32 bits wide
  assign xor_1_out = A ^ B;  // XOR_Gate xor_1, 32 bits wide
  Shifter #(.width(32)) shifter_1 (.in(B), .\dist (Shift), .out(shifter_1_out));
  Shifter #(.shift("lr"), .width(32)) shifter_2 (.in(B), .\dist (Shift), .out(shifter_2_out));
  Shifter #(.shift("ar"), .width(32)) shifter_3 (.in(B), .\dist (Shift), .out(shifter_3_out));
  Adder #(.width(32)) adder_1 (.a(A), .b(B), .out(adder_1_out), .cin(CarryIn), .cout(ADC_OUT));
  Subtractor #(.width(32)) subtractor_1 (.a(B), .b(A), .out(subtractor_1_out), .bin(not_1_out), .bout(SBC_OUT));
  Shifter #(.shift("rr"), .width(32)) shifter_4 (.in(B), .\dist (Shift), .out(shifter_4_out));
  assign CMN = A & B;  // AND_Gate and_2, 32 bits wide
  Subtractor #(.width(32)) subtractor_2 (.a({32{1'b0}}), .b(A), .out(subtractor_2_out), .bout(RSB_OUT));  // open: bin
  Subtractor #(.width(32)) subtractor_3 (.a(B), .b(A), .out(CMN), .bout(CMP_OUT));  // open: bin
  Adder #(.width(32)) adder_2 (.a(A), .b(B), .out(CMN), .cout(CMN_OUT));  // open: cin
  assign or_1_out = A | B;  // OR_Gate or_1, 32 bits wide
  Multiplier #(.width(32)) multiplier_1 (.a(A), .b(B), .out(multiplier_1_out));  // open: cin, cout
  assign and_3_out = not_2_out & B;  // AND_Gate and_3, 32 bits wide
  assign not_3_out = ~A;  // NOT_Gate not_3, 32 bits wide
  BitSelector #(.width(32)) bitselector_1 (.in(B), .out(bitselector_1_out), .sel({5{1'b1}}));
  BitSelector #(.width(32)) bitselector_2 (.in(A), .out(bitselector_2_out), .sel({5{1'b1}}));
  BitSelector #(.width(32)) bitselector_3 (.in(S), .out(bitselector_3_out), .sel({5{1'b1}}));
  Subtractor #(.width(5)) subtractor_4 (.a(Shift), .b(5'b00001), .out(subtractor_4_out));  // open: bin, bout
  Subtractor #(.width(5)) subtractor_5 (.a({5{1'b0}}), .b(Shift), .out(subtractor_5_out));  // open: bin, bout
  BitSelector #(.width(32)) bitselector_4 (.in(B), .out(bitselector_4_out), .sel(subtractor_4_out));
  BitSelector #(.width(32)) bitselector_5 (.in(B), .out(bitselector_5_out), .sel(subtractor_5_out));
  V_FLAG_ADD v_flag_add_1 (.A(bitselector_2_out), .B(bitselector_1_out), .S(bitselector_3_out), .V(v_flag_add_1_v));
  V_FLAG_SUB v_flag_sub_1 (.A(bitselector_2_out), .B(bitselector_1_out), .S(bitselector_3_out), .V(v_flag_sub_1_v));
  Multiplexer #(.select(4), .width(32)) multiplexer_1 (
    .in0(and_1_out), .in1(xor_1_out), .in2(shifter_1_out), .in3(shifter_2_out), .in4(shifter_3_out),
    .in5(adder_1_out), .in6(subtractor_1_out), .in7(shifter_4_out), .in8(B), .in9(subtractor_2_out),
    .in10(B), .in11(B), .in12(or_1_out), .in13(multiplier_1_out), .in14(and_3_out), .in15(not_3_out),
    .out(S), .sel(Codop));
  Multiplexer #(.select(4)) multiplexer_2 (
    .in0(1'b0), .in1(1'b0), .in2(bitselector_5_out), .in3(bitselector_4_out), .in4(bitselector_4_out),
    .in5(ADC_OUT), .in6(SBC_OUT), .in7(bitselector_4_out), .in8(1'b0), .in9(RSB_OUT), .in10(CMP_OUT),
    .in11(CMN_OUT), .in12(1'b0), .in13(1'b0), .in14(1'b0), .in15(1'b0), .out(Flags[2]), .sel(Codop));
  Multiplexer #(.select(4)) multiplexer_3 (
    .in0(1'b0), .in1(1'b0), .in2(1'b0), .in3(1'b0), .in4(1'b0), .in5(v_flag_add_1_v), .in6(v_flag_sub_1_v),
    .in7(1'b0), .in8(1'b0), .in9(1'b0), .in10(1'b0), .in11(1'b0), .in12(1'b0), .in13(1'b0), .in14(1'b0),
    .in15(1'b0), .out(Flags[3]), .sel(Codop));
  Comparator #(.width(32)) comparator_1 (.a(S), .b({32{1'b0}}), .eq(Flags[1]), .lt(Flags[0]));  // open: gt
  // also tied to GND on the sheet: {CMN[0], CMN[1], CMN[2], CMN[3], CMN[4], CMN[5], CMN[6], CMN[7], CMN[8], CMN[9], CMN[10], CMN[11], CMN[12], CMN[13], CMN[14], CMN[15], CMN[16], CMN[17], CMN[18], CMN[19], CMN[20], CMN[21], CMN[22], CMN[23], CMN[24], CMN[25], CMN[26], CMN[27], CMN[28], CMN[29], CMN[30], CMN[31]}

  // Other names for the same wires on the sheet: N = Flags[0]; Z = Flags[1]; C = Flags[2]; V = Flags[3];
  //   SH[4:0] = Shift; CMP[31:0] = CMN; TST[31:0] = CMN

  // Notes on the sheet:
  //   A
  //   B
  //   Sh
  //   Note: for ROR, C = N
  //   Note 2: assume that shift > 0 for LSL and LSR
endmodule

module V_FLAG_SUB (
  input  A,
  input  B,
  input  S,
  output V
);

  wire and_1_out, and_2_out, not_1_out, not_2_out, not_3_out;

  not not_1 (not_1_out, A);
  not not_2 (not_2_out, B);
  not not_3 (not_3_out, S);
  and and_1 (and_1_out, not_1_out, B, S);
  or or_1 (V, and_1_out, and_2_out);
  and and_2 (and_2_out, A, not_2_out, not_3_out);
endmodule

module V_FLAG_ADD (
  input  A,
  input  B,
  input  S,
  output V
);

  wire and_1_out, and_2_out, not_1_out, not_2_out, not_3_out;

  not not_1 (not_1_out, A);
  not not_2 (not_2_out, B);
  not not_3 (not_3_out, S);
  and and_1 (and_1_out, not_1_out, not_2_out, S);
  or or_1 (V, and_1_out, and_2_out);
  and and_2 (and_2_out, A, B, not_3_out);
endmodule
