// Logisim project Ctl_Opcode_Decoder.circ as structural Verilog: 1 circuit, main circuit Opcode_Decoder
module Opcode_Decoder (
  input  [5:0] Opcode,
  output Shift,
  output Data_Processing,
  output Load_Store,
  output SP_Address,
  output Conditional
);

  wire and_1_out, not_1_out, not_2_out, not_3_out, not_4_out, not_5_out;

  not not_1 (not_1_out, Opcode[4]);
  and and_1 (and_1_out, Opcode[5], not_1_out);
  not not_2 (not_2_out, Opcode[4]);
  and and_2 (Shift, not_2_out, not_3_out);
  not not_3 (not_3_out, Opcode[5]);
  not not_4 (not_4_out, Opcode[5]);
  and and_3 (Data_Processing, not_4_out, Opcode[4]);
  and and_4 (Load_Store, and_1_out, not_5_out);
  not not_5 (not_5_out, Opcode[3]);
  and and_5 (SP_Address, and_1_out, Opcode[3]);
  and and_6 (Conditional, Opcode[5], Opcode[4]);

  // Notes on the sheet:
  //   Shift, add, sub, mov
  //   Load/Store
  //   SP Address
  //   Conditional branch
  //   Data Processing
endmodule
